// Logisim project subleq CPU.circ as structural Verilog: 1 circuit, main circuit main
module main (
  input  RESET
);

  wire and_1_out, and_2_out, and_3_out, and_4_out, and_5_out, and_6_out, and_7_out, and_8_out, and_9_out,
       and_10_out, and_11_out, and_12_out, and_13_out, and_14_out, and_15_out, and_16_out, and_17_out,
       and_18_out, and_19_out, and_20_out, and_21_out, and_22_out, and_23_out, and_24_out, and_25_out,
       and_26_out, and_27_out, and_28_out, and_29_out, and_30_out, and_31_out, and_33_out, and_34_out,
       and_35_out, and_36_out, and_37_out, and_38_out, and_39_out, and_40_out, and_41_out, and_42_out,
       and_43_out, and_44_out, and_45_out, and_46_out, and_47_out, clock_1_out, nand_1_out, nand_2_out,
       nand_3_out, nand_4_out, nand_5_out, nand_6_out, nand_7_out, nand_8_out, nand_9_out, nand_10_out,
       nand_11_out, nand_12_out, nand_13_out, nand_14_out, nand_15_out, nand_16_out, nand_17_out,
       nand_18_out, nand_19_out, nand_20_out, nand_21_out, nand_22_out, nand_23_out, nand_24_out,
       nand_25_out, nand_26_out, nand_27_out, nand_28_out, nand_29_out, nand_30_out, nand_31_out,
       nand_32_out, nand_33_out, nand_34_out, nand_35_out, nand_36_out, nand_37_out, nand_38_out,
       nand_39_out, nand_40_out, nand_41_out, nand_42_out, nand_43_out, nand_44_out, nand_45_out,
       nand_46_out, nand_47_out, nand_48_out, nand_49_out, nand_50_out, nand_51_out, nand_52_out,
       nand_53_out, nand_54_out, nand_55_out, nand_56_out, nand_57_out, nand_58_out, nand_59_out,
       nand_60_out, nand_61_out, nand_62_out, nand_63_out, nand_64_out, nand_73_out, nand_74_out,
       nand_75_out, nand_76_out, nand_77_out, nand_78_out, nand_79_out, nand_80_out, nand_81_out,
       nand_82_out, nand_83_out, nand_84_out, nand_85_out, nand_86_out, nand_87_out, nand_88_out,
       nand_89_out, nand_90_out, nand_91_out, nand_92_out, nand_93_out, nand_94_out, nand_95_out,
       nand_96_out, nand_97_out, nand_98_out, nand_99_out, nand_100_out, nand_101_out, nand_102_out,
       nand_103_out, nand_104_out, nand_105_out, nand_106_out, nor_1_out, nor_2_out, nor_3_out, nor_4_out,
       nor_5_out, nor_6_out, nor_7_out, nor_8_out, nor_9_out, nor_10_out, nor_11_out, nor_12_out, nor_13_out,
       nor_14_out, nor_15_out, nor_16_out, nor_17_out, nor_18_out, nor_19_out, nor_20_out, nor_21_out,
       nor_22_out, nor_23_out, nor_24_out, nor_25_out, nor_26_out, nor_27_out, nor_28_out, nor_29_out,
       nor_30_out, nor_31_out, nor_32_out, nor_33_out, nor_34_out, nor_35_out, nor_36_out, nor_37_out,
       nor_38_out, nor_39_out, nor_40_out, nor_41_out, nor_42_out, nor_43_out, nor_44_out, nor_45_out,
       nor_46_out, nor_47_out, nor_48_out, nor_49_out, nor_50_out, nor_51_out, nor_52_out, nor_53_out,
       nor_54_out, nor_55_out, nor_56_out, nor_57_out, nor_58_out, nor_59_out, nor_60_out, nor_61_out,
       nor_62_out, nor_63_out, nor_64_out, nor_65_out, nor_66_out, nor_67_out, nor_68_out, nor_69_out,
       nor_70_out, nor_71_out, nor_72_out, nor_73_out, nor_74_out, nor_75_out, nor_76_out, nor_77_out,
       nor_78_out, nor_79_out, nor_80_out, nor_81_out, nor_82_out, nor_83_out, nor_84_out, nor_85_out,
       nor_86_out, nor_87_out, nor_88_out, nor_89_out, nor_90_out, nor_91_out, nor_92_out, nor_93_out,
       nor_94_out, nor_95_out, nor_96_out, nor_97_out, nor_98_out, nor_99_out, nor_100_out, nor_101_out,
       nor_102_out, nor_103_out, nor_104_out, nor_105_out, nor_106_out, nor_107_out, nor_108_out,
       nor_109_out, nor_110_out, nor_111_out, nor_112_out, nor_113_out, nor_114_out, nor_115_out,
       nor_116_out, nor_117_out, not_1_out, not_2_out, not_3_out, not_4_out, not_5_out, not_6_out, or_1_out,
       or_2_out, or_3_out, or_4_out, xnor_1_out, xnor_2_out, xnor_3_out, xnor_4_out, xnor_5_out, xnor_6_out,
       xnor_7_out, xnor_8_out, xnor_9_out, xnor_10_out, xnor_11_out, xnor_12_out, xnor_13_out, xnor_14_out,
       xnor_15_out, xor_1_out, xor_2_out, xor_3_out, xor_4_out, xor_5_out, xor_6_out, xor_7_out, xor_8_out;
  wire [3:0] bitselector_1_out, bitselector_2_out, bitselector_3_out;
  wire [7:0] controlled_buffer_1_out, divider_1_out, divider_1_rem, divider_2_out, divider_2_rem,
       divider_3_rem, nand_107_out, pull_resistor_8_node, register_1_q;

  Pull_Resistor #(.pull(1)) pull_resistor_1 (.node(pull_resistor_8_node[0]));
  Pull_Resistor #(.pull(1)) pull_resistor_2 (.node(pull_resistor_8_node[1]));
  Pull_Resistor #(.pull(1)) pull_resistor_3 (.node(pull_resistor_8_node[2]));
  Pull_Resistor #(.pull(1)) pull_resistor_4 (.node(pull_resistor_8_node[3]));
  Pull_Resistor #(.pull(1)) pull_resistor_5 (.node(pull_resistor_8_node[4]));
  Pull_Resistor #(.pull(1)) pull_resistor_6 (.node(pull_resistor_8_node[5]));
  Pull_Resistor #(.pull(1)) pull_resistor_7 (.node(pull_resistor_8_node[6]));
  Pull_Resistor #(.pull(1)) pull_resistor_8 (.node(pull_resistor_8_node[7]));
  not not_1 (not_1_out, nor_109_out);
  nor nor_1 (nor_1_out, not_1_out, clock_1_out);
  nand nand_1 (nand_1_out, pull_resistor_8_node[0], nor_1_out);
  nand nand_2 (nand_2_out, nand_1_out, nor_1_out);
  nand nand_3 (nand_3_out, pull_resistor_8_node[1], nor_1_out);
  nand nand_4 (nand_4_out, nand_3_out, nor_1_out);
  nand nand_5 (nand_5_out, pull_resistor_8_node[2], nor_1_out);
  nand nand_6 (nand_6_out, nand_5_out, nor_1_out);
  nand nand_7 (nand_7_out, pull_resistor_8_node[3], nor_1_out);
  nand nand_8 (nand_8_out, nand_7_out, nor_1_out);
  nand nand_9 (nand_9_out, pull_resistor_8_node[4], nor_1_out);
  nand nand_10 (nand_10_out, nand_9_out, nor_1_out);
  nand nand_11 (nand_11_out, pull_resistor_8_node[5], nor_1_out);
  nand nand_12 (nand_12_out, nand_11_out, nor_1_out);
  nand nand_13 (nand_13_out, pull_resistor_8_node[6], nor_1_out);
  nand nand_14 (nand_14_out, nand_13_out, nor_1_out);
  nand nand_15 (nand_15_out, pull_resistor_8_node[7], nor_1_out);
  nand nand_16 (nand_16_out, nand_15_out, nor_1_out);
  nand nand_17 (nand_17_out, nand_1_out, nand_18_out);
  nand nand_18 (nand_18_out, nand_17_out, nand_2_out);
  nand nand_19 (nand_19_out, nand_3_out, nand_20_out);
  nand nand_20 (nand_20_out, nand_19_out, nand_4_out);
  nand nand_21 (nand_21_out, nand_5_out, nand_22_out);
  nand nand_22 (nand_22_out, nand_21_out, nand_6_out);
  nand nand_23 (nand_23_out, nand_7_out, nand_24_out);
  nand nand_24 (nand_24_out, nand_23_out, nand_8_out);
  nand nand_25 (nand_25_out, nand_9_out, nand_26_out);
  nand nand_26 (nand_26_out, nand_25_out, nand_10_out);
  nand nand_27 (nand_27_out, nand_11_out, nand_28_out);
  nand nand_28 (nand_28_out, nand_27_out, nand_12_out);
  nand nand_29 (nand_29_out, nand_13_out, nand_30_out);
  nand nand_30 (nand_30_out, nand_29_out, nand_14_out);
  nand nand_31 (nand_31_out, nand_15_out, nand_32_out);
  nand nand_32 (nand_32_out, nand_31_out, nand_16_out);
  not not_2 (not_2_out, nor_113_out);
  nor nor_2 (nor_2_out, not_2_out, clock_1_out);
  nand nand_33 (nand_33_out, pull_resistor_8_node[0], nor_2_out);
  nand nand_34 (nand_34_out, nand_33_out, nor_2_out);
  nand nand_35 (nand_35_out, pull_resistor_8_node[1], nor_2_out);
  nand nand_36 (nand_36_out, nand_35_out, nor_2_out);
  nand nand_37 (nand_37_out, pull_resistor_8_node[2], nor_2_out);
  nand nand_38 (nand_38_out, nand_37_out, nor_2_out);
  nand nand_39 (nand_39_out, pull_resistor_8_node[3], nor_2_out);
  nand nand_40 (nand_40_out, nand_39_out, nor_2_out);
  nand nand_41 (nand_41_out, pull_resistor_8_node[4], nor_2_out);
  nand nand_42 (nand_42_out, nand_41_out, nor_2_out);
  nand nand_43 (nand_43_out, pull_resistor_8_node[5], nor_2_out);
  nand nand_44 (nand_44_out, nand_43_out, nor_2_out);
  nand nand_45 (nand_45_out, pull_resistor_8_node[6], nor_2_out);
  nand nand_46 (nand_46_out, nand_45_out, nor_2_out);
  nand nand_47 (nand_47_out, pull_resistor_8_node[7], nor_2_out);
  nand nand_48 (nand_48_out, nand_47_out, nor_2_out);
  nand nand_49 (nand_49_out, nand_33_out, nand_50_out);
  nand nand_50 (nand_50_out, nand_49_out, nand_34_out);
  nand nand_51 (nand_51_out, nand_35_out, nand_52_out);
  nand nand_52 (nand_52_out, nand_51_out, nand_36_out);
  nand nand_53 (nand_53_out, nand_37_out, nand_54_out);
  nand nand_54 (nand_54_out, nand_53_out, nand_38_out);
  nand nand_55 (nand_55_out, nand_39_out, nand_56_out);
  nand nand_56 (nand_56_out, nand_55_out, nand_40_out);
  nand nand_57 (nand_57_out, nand_41_out, nand_58_out);
  nand nand_58 (nand_58_out, nand_57_out, nand_42_out);
  nand nand_59 (nand_59_out, nand_43_out, nand_60_out);
  nand nand_60 (nand_60_out, nand_59_out, nand_44_out);
  nand nand_61 (nand_61_out, nand_45_out, nand_62_out);
  nand nand_62 (nand_62_out, nand_61_out, nand_46_out);
  nand nand_63 (nand_63_out, nand_47_out, nand_64_out);
  nand nand_64 (nand_64_out, nand_63_out, nand_48_out);
  xor xor_1 (xor_1_out, nand_18_out, nand_49_out);
  nor nor_3 (nor_3_out, nand_18_out, nand_49_out);
  not not_3 (not_3_out, nor_3_out);
  xnor xnor_1 (xnor_1_out, nand_20_out, nand_51_out);
  nor nor_4 (nor_4_out, nand_20_out, nand_51_out);
  xnor xnor_2 (xnor_2_out, nand_22_out, nand_53_out);
  nor nor_5 (nor_5_out, nand_22_out, nand_53_out);
  xnor xnor_3 (xnor_3_out, nand_24_out, nand_55_out);
  nor nor_6 (nor_6_out, nand_24_out, nand_55_out);
  xnor xnor_4 (xnor_4_out, nand_26_out, nand_57_out);
  nor nor_7 (nor_7_out, nand_26_out, nand_57_out);
  xnor xnor_5 (xnor_5_out, nand_28_out, nand_59_out);
  nor nor_8 (nor_8_out, nand_28_out, nand_59_out);
  xnor xnor_6 (xnor_6_out, nand_30_out, nand_61_out);
  nor nor_9 (nor_9_out, nand_30_out, nand_61_out);
  xnor xnor_7 (xnor_7_out, nand_32_out, nand_63_out);
  xor xor_2 (xor_2_out, not_3_out, xnor_1_out);
  nor nor_10 (nor_10_out, not_3_out, xnor_1_out);
  xor xor_3 (xor_3_out, nor_16_out, xnor_2_out);
  nor nor_11 (nor_11_out, nor_16_out, xnor_2_out);
  xor xor_4 (xor_4_out, nor_17_out, xnor_3_out);
  nor nor_12 (nor_12_out, nor_17_out, xnor_3_out);
  xor xor_5 (xor_5_out, nor_18_out, xnor_4_out);
  nor nor_13 (nor_13_out, nor_18_out, xnor_4_out);
  xor xor_6 (xor_6_out, nor_19_out, xnor_5_out);
  nor nor_14 (nor_14_out, nor_19_out, xnor_5_out);
  xor xor_7 (xor_7_out, nor_20_out, xnor_6_out);
  nor nor_15 (nor_15_out, nor_20_out, xnor_6_out);
  xor xor_8 (xor_8_out, nor_21_out, xnor_7_out);
  nor nor_16 (nor_16_out, nor_10_out, nor_4_out);
  nor nor_17 (nor_17_out, nor_11_out, nor_5_out);
  nor nor_18 (nor_18_out, nor_12_out, nor_6_out);
  nor nor_19 (nor_19_out, nor_13_out, nor_7_out);
  nor nor_20 (nor_20_out, nor_14_out, nor_8_out);
  nor nor_21 (nor_21_out, nor_15_out, nor_9_out);
  nand nand_65 (pull_resistor_8_node[0], xor_1_out, nor_115_out);
  nand nand_66 (pull_resistor_8_node[1], xor_2_out, nor_115_out);
  nand nand_67 (pull_resistor_8_node[2], xor_3_out, nor_115_out);
  nand nand_68 (pull_resistor_8_node[3], xor_4_out, nor_115_out);
  nand nand_69 (pull_resistor_8_node[4], xor_5_out, nor_115_out);
  nand nand_70 (pull_resistor_8_node[5], xor_6_out, nor_115_out);
  nand nand_71 (pull_resistor_8_node[6], xor_7_out, nor_115_out);
  nand nand_72 (pull_resistor_8_node[7], xor_8_out, nor_115_out);
  nand nand_73 (nand_73_out, xor_1_out, xor_2_out, xor_3_out, xor_4_out, xor_5_out, xor_6_out, xor_7_out, xor_8_out);
  nand nand_74 (nand_74_out, nand_73_out, xor_8_out);
  nor nor_22 (nor_22_out, nor_111_out, nor_107_out);
  nor nor_23 (nor_23_out, nor_22_out, clock_1_out);
  nand nand_75 (nand_75_out, pull_resistor_8_node[0], nor_23_out);
  nand nand_76 (nand_76_out, nand_75_out, nor_23_out);
  nand nand_77 (nand_77_out, pull_resistor_8_node[1], nor_23_out);
  nand nand_78 (nand_78_out, nand_77_out, nor_23_out);
  nand nand_79 (nand_79_out, pull_resistor_8_node[2], nor_23_out);
  nand nand_80 (nand_80_out, nand_79_out, nor_23_out);
  nand nand_81 (nand_81_out, pull_resistor_8_node[3], nor_23_out);
  nand nand_82 (nand_82_out, nand_81_out, nor_23_out);
  nand nand_83 (nand_83_out, pull_resistor_8_node[4], nor_23_out);
  nand nand_84 (nand_84_out, nand_83_out, nor_23_out);
  nand nand_85 (nand_85_out, pull_resistor_8_node[5], nor_23_out);
  nand nand_86 (nand_86_out, nand_85_out, nor_23_out);
  nand nand_87 (nand_87_out, pull_resistor_8_node[6], nor_23_out);
  nand nand_88 (nand_88_out, nand_87_out, nor_23_out);
  nand nand_89 (nand_89_out, pull_resistor_8_node[7], nor_23_out);
  nand nand_90 (nand_90_out, nand_89_out, nor_23_out);
  or or_1 (or_1_out, nor_115_out, nor_113_out, nor_109_out);
  nand nand_91 (nand_91_out, nand_75_out, nand_92_out);
  nand nand_92 (nand_92_out, nand_91_out, nand_76_out);
  nand nand_93 (nand_93_out, nand_77_out, nand_94_out);
  nand nand_94 (nand_94_out, nand_93_out, nand_78_out);
  nand nand_95 (nand_95_out, nand_79_out, nand_96_out);
  nand nand_96 (nand_96_out, nand_95_out, nand_80_out);
  nand nand_97 (nand_97_out, nand_81_out, nand_98_out);
  nand nand_98 (nand_98_out, nand_97_out, nand_82_out);
  nand nand_99 (nand_99_out, nand_83_out, nand_100_out);
  nand nand_100 (nand_100_out, nand_99_out, nand_84_out);
  nand nand_101 (nand_101_out, nand_85_out, nand_102_out);
  nand nand_102 (nand_102_out, nand_101_out, nand_86_out);
  nand nand_103 (nand_103_out, nand_87_out, nand_104_out);
  nand nand_104 (nand_104_out, nand_103_out, nand_88_out);
  nand nand_105 (nand_105_out, nand_89_out, nand_106_out);
  nand nand_106 (nand_106_out, nand_105_out, nand_90_out);
  nand nand_107 (nand_107_out[0], or_1_out, nand_92_out);
  nand nand_108 (nand_107_out[1], or_1_out, nand_94_out);
  nand nand_109 (nand_107_out[2], or_1_out, nand_96_out);
  nand nand_110 (nand_107_out[3], or_1_out, nand_98_out);
  nand nand_111 (nand_107_out[4], or_1_out, nand_100_out);
  nand nand_112 (nand_107_out[5], or_1_out, nand_102_out);
  nand nand_113 (nand_107_out[6], or_1_out, nand_104_out);
  nand nand_114 (nand_107_out[7], or_1_out, nand_106_out);
  Pull_Resistor #(.pull(1)) pull_resistor_9 (.node(nand_107_out[0]));
  Pull_Resistor #(.pull(1)) pull_resistor_10 (.node(nand_107_out[1]));
  Pull_Resistor #(.pull(1)) pull_resistor_11 (.node(nand_107_out[2]));
  Pull_Resistor #(.pull(1)) pull_resistor_12 (.node(nand_107_out[3]));
  Pull_Resistor #(.pull(1)) pull_resistor_13 (.node(nand_107_out[4]));
  Pull_Resistor #(.pull(1)) pull_resistor_14 (.node(nand_107_out[5]));
  Pull_Resistor #(.pull(1)) pull_resistor_15 (.node(nand_107_out[6]));
  Pull_Resistor #(.pull(1)) pull_resistor_16 (.node(nand_107_out[7]));
  nor nor_24 (nor_24_out, xnor_8_out, and_46_out);
  and and_1 (and_1_out, and_46_out, pull_resistor_8_node[0]);
  nor nor_25 (nor_25_out, xnor_9_out, and_46_out);
  and and_2 (and_2_out, and_46_out, pull_resistor_8_node[1]);
  nor nor_26 (nor_26_out, xnor_10_out, and_46_out);
  and and_3 (and_3_out, and_46_out, pull_resistor_8_node[2]);
  nor nor_27 (nor_27_out, xnor_11_out, and_46_out);
  and and_4 (and_4_out, and_46_out, pull_resistor_8_node[3]);
  nor nor_28 (nor_28_out, xnor_12_out, and_46_out);
  and and_5 (and_5_out, and_46_out, pull_resistor_8_node[4]);
  nor nor_29 (nor_29_out, xnor_13_out, and_46_out);
  and and_6 (and_6_out, and_46_out, pull_resistor_8_node[5]);
  nor nor_30 (nor_30_out, xnor_14_out, and_46_out);
  and and_7 (and_7_out, and_46_out, pull_resistor_8_node[6]);
  nor nor_31 (nor_31_out, xnor_15_out, and_46_out);
  and and_8 (and_8_out, and_46_out, pull_resistor_8_node[7]);
  nor nor_32 (nor_32_out, nor_24_out, and_1_out, clock_1_out);
  nor nor_33 (nor_33_out, nor_32_out, clock_1_out);
  nor nor_34 (nor_34_out, nor_25_out, and_2_out, clock_1_out);
  nor nor_35 (nor_35_out, nor_34_out, clock_1_out);
  nor nor_36 (nor_36_out, nor_26_out, and_3_out, clock_1_out);
  nor nor_37 (nor_37_out, nor_36_out, clock_1_out);
  nor nor_38 (nor_38_out, nor_27_out, and_4_out, clock_1_out);
  nor nor_39 (nor_39_out, nor_38_out, clock_1_out);
  nor nor_40 (nor_40_out, nor_28_out, and_5_out, clock_1_out);
  nor nor_41 (nor_41_out, nor_40_out, clock_1_out);
  nor nor_42 (nor_42_out, nor_29_out, and_6_out, clock_1_out);
  nor nor_43 (nor_43_out, nor_42_out, clock_1_out);
  nor nor_44 (nor_44_out, nor_30_out, and_7_out, clock_1_out);
  nor nor_45 (nor_45_out, nor_44_out, clock_1_out);
  nor nor_46 (nor_46_out, nor_31_out, and_8_out, clock_1_out);
  nor nor_47 (nor_47_out, nor_46_out, clock_1_out);
  nor nor_48 (nor_48_out, nor_32_out, RESET, nor_49_out);
  nor nor_49 (nor_49_out, nor_48_out, nor_33_out);
  nor nor_50 (nor_50_out, nor_34_out, RESET, nor_51_out);
  nor nor_51 (nor_51_out, nor_50_out, nor_35_out);
  nor nor_52 (nor_52_out, nor_36_out, RESET, nor_53_out);
  nor nor_53 (nor_53_out, nor_52_out, nor_37_out);
  nor nor_54 (nor_54_out, nor_38_out, RESET, nor_55_out);
  nor nor_55 (nor_55_out, nor_54_out, nor_39_out);
  nor nor_56 (nor_56_out, nor_40_out, RESET, nor_57_out);
  nor nor_57 (nor_57_out, nor_56_out, nor_41_out);
  nor nor_58 (nor_58_out, nor_42_out, RESET, nor_59_out);
  nor nor_59 (nor_59_out, nor_58_out, nor_43_out);
  nor nor_60 (nor_60_out, nor_44_out, RESET, nor_61_out);
  nor nor_61 (nor_61_out, nor_60_out, nor_45_out);
  nor nor_62 (nor_62_out, nor_46_out, RESET, nor_63_out);
  nor nor_63 (nor_63_out, nor_62_out, nor_47_out);
  and and_9 (and_9_out, nor_48_out, clock_1_out);
  and and_10 (and_10_out, clock_1_out, nor_49_out);
  and and_11 (and_11_out, nor_50_out, clock_1_out);
  and and_12 (and_12_out, clock_1_out, nor_51_out);
  and and_13 (and_13_out, nor_52_out, clock_1_out);
  and and_14 (and_14_out, clock_1_out, nor_53_out);
  and and_15 (and_15_out, nor_54_out, clock_1_out);
  and and_16 (and_16_out, clock_1_out, nor_55_out);
  and and_17 (and_17_out, nor_56_out, clock_1_out);
  and and_18 (and_18_out, clock_1_out, nor_57_out);
  and and_19 (and_19_out, nor_58_out, clock_1_out);
  and and_20 (and_20_out, clock_1_out, nor_59_out);
  and and_21 (and_21_out, nor_60_out, clock_1_out);
  and and_22 (and_22_out, clock_1_out, nor_61_out);
  and and_23 (and_23_out, nor_62_out, clock_1_out);
  and and_24 (and_24_out, clock_1_out, nor_63_out);
  nor nor_64 (nor_64_out, and_9_out, nor_65_out);
  nor nor_65 (nor_65_out, nor_64_out, RESET, and_10_out);
  nor nor_66 (nor_66_out, and_11_out, nor_67_out);
  nor nor_67 (nor_67_out, nor_66_out, RESET, and_12_out);
  nor nor_68 (nor_68_out, and_13_out, nor_69_out);
  nor nor_69 (nor_69_out, nor_68_out, RESET, and_14_out);
  nor nor_70 (nor_70_out, and_15_out, nor_71_out);
  nor nor_71 (nor_71_out, nor_70_out, RESET, and_16_out);
  nor nor_72 (nor_72_out, and_17_out, nor_73_out);
  nor nor_73 (nor_73_out, nor_72_out, RESET, and_18_out);
  nor nor_74 (nor_74_out, and_19_out, nor_75_out);
  nor nor_75 (nor_75_out, nor_74_out, RESET, and_20_out);
  nor nor_76 (nor_76_out, and_21_out, nor_77_out);
  nor nor_77 (nor_77_out, nor_76_out, RESET, and_22_out);
  nor nor_78 (nor_78_out, and_23_out, nor_79_out);
  nor nor_79 (nor_79_out, nor_78_out, RESET, and_24_out);
  or or_2 (or_2_out, and_47_out, nor_111_out, nor_107_out);
  xnor xnor_8 (xnor_8_out, or_2_out, nor_65_out);
  and and_25 (and_25_out, or_2_out, nor_65_out);
  xnor xnor_9 (xnor_9_out, and_25_out, nor_67_out);
  and and_26 (and_26_out, and_25_out, nor_67_out);
  xnor xnor_10 (xnor_10_out, and_26_out, nor_69_out);
  and and_27 (and_27_out, and_26_out, nor_69_out);
  xnor xnor_11 (xnor_11_out, and_27_out, nor_71_out);
  and and_28 (and_28_out, and_27_out, nor_71_out);
  xnor xnor_12 (xnor_12_out, and_28_out, nor_73_out);
  and and_29 (and_29_out, and_28_out, nor_73_out);
  xnor xnor_13 (xnor_13_out, and_29_out, nor_75_out);
  and and_30 (and_30_out, and_29_out, nor_75_out);
  xnor xnor_14 (xnor_14_out, and_30_out, nor_77_out);
  and and_31 (and_31_out, and_30_out, nor_77_out);
  xnor xnor_15 (xnor_15_out, and_31_out, nor_79_out);
  // AND_Gate and_32 has open pins: in0=and_31_out, in1=nor_79_out, out=open
  or or_3 (or_3_out, and_46_out, nor_111_out, nor_107_out);
  nand nand_115 (nand_107_out[0], nor_64_out, or_3_out);
  nand nand_116 (nand_107_out[1], nor_66_out, or_3_out);
  nand nand_117 (nand_107_out[2], nor_68_out, or_3_out);
  nand nand_118 (nand_107_out[3], nor_70_out, or_3_out);
  nand nand_119 (nand_107_out[4], nor_72_out, or_3_out);
  nand OC (nand_107_out[5], nor_74_out, or_3_out);
  nand nand_120 (nand_107_out[6], nor_76_out, or_3_out);
  nand nand_121 (nand_107_out[7], nor_78_out, or_3_out);
  not not_4 (not_4_out, nor_115_out);
  nor nor_80 (nor_80_out, and_47_out, nor_115_out, clock_1_out);
  nor nor_81 (nor_81_out, not_4_out, clock_1_out);
  and and_33 (and_33_out, nand_107_out[0], nand_107_out[1], nand_107_out[2], nand_107_out[3], nor_81_out, nand_107_out[4], nand_107_out[5], nand_107_out[6], nand_107_out[7]);
  Clock clock_1 (.out(clock_1_out));
  assign controlled_buffer_1_out = or_4_out ? nand_107_out : 8'bz;  // Controlled_Buffer controlled_buffer_1
  not not_5 (not_5_out, nor_80_out);
  or or_4 (or_4_out, nor_81_out, nor_80_out);
  nor nor_82 (nor_82_out, nor_117_out, clock_1_out);
  nor nor_83 (nor_83_out, nor_82_out, clock_1_out);
  nor nor_84 (nor_84_out, nor_107_out, clock_1_out);
  nor nor_85 (nor_85_out, nor_84_out, clock_1_out);
  nor nor_86 (nor_86_out, nor_109_out, clock_1_out);
  nor nor_87 (nor_87_out, nor_86_out, clock_1_out);
  nor nor_88 (nor_88_out, nor_111_out, clock_1_out);
  nor nor_89 (nor_89_out, nor_88_out, clock_1_out);
  nor nor_90 (nor_90_out, nor_113_out, clock_1_out);
  nor nor_91 (nor_91_out, nor_90_out, clock_1_out);
  nor nor_92 (nor_92_out, nor_115_out, clock_1_out);
  nor nor_93 (nor_93_out, nor_92_out, clock_1_out);
  RAM #(.databus("bidir"), .trigger("high")) ram_1 (
    .addr(controlled_buffer_1_out), .we(not_5_out), .oe(nor_80_out), .data(pull_resistor_8_node));
  nor nor_94 (nor_94_out, nor_82_out, nor_95_out);
  and and_34 (and_34_out, nor_94_out, clock_1_out);
  nor nor_95 (nor_95_out, nor_94_out, RESET, nor_83_out);
  and and_35 (and_35_out, clock_1_out, nor_95_out);
  nor nor_96 (nor_96_out, nor_84_out, RESET, nor_97_out);
  and and_36 (and_36_out, nor_96_out, clock_1_out);
  nor nor_97 (nor_97_out, nor_96_out, nor_85_out);
  and and_37 (and_37_out, clock_1_out, nor_97_out);
  nor nor_98 (nor_98_out, nor_86_out, RESET, nor_99_out);
  and and_38 (and_38_out, nor_98_out, clock_1_out);
  nor nor_99 (nor_99_out, nor_98_out, nor_87_out);
  and and_39 (and_39_out, clock_1_out, nor_99_out);
  nor nor_100 (nor_100_out, nor_88_out, RESET, nor_101_out);
  and and_40 (and_40_out, nor_100_out, clock_1_out);
  nor nor_101 (nor_101_out, nor_100_out, nor_89_out);
  and and_41 (and_41_out, clock_1_out, nor_101_out);
  nor nor_102 (nor_102_out, nor_90_out, RESET, nor_103_out);
  and and_42 (and_42_out, nor_102_out, clock_1_out);
  nor nor_103 (nor_103_out, nor_102_out, nor_91_out);
  and and_43 (and_43_out, clock_1_out, nor_103_out);
  nor nor_104 (nor_104_out, nor_92_out, RESET, nor_105_out);
  and and_44 (and_44_out, nor_104_out, clock_1_out);
  nor nor_105 (nor_105_out, nor_104_out, nor_93_out);
  and and_45 (and_45_out, clock_1_out, nor_105_out);
  nor nor_106 (nor_106_out, and_34_out, RESET, nor_107_out);
  nor nor_107 (nor_107_out, nor_106_out, and_35_out);
  nor nor_108 (nor_108_out, and_36_out, nor_109_out);
  nor nor_109 (nor_109_out, nor_108_out, RESET, and_37_out);
  nor nor_110 (nor_110_out, and_38_out, nor_111_out);
  nor nor_111 (nor_111_out, nor_110_out, RESET, and_39_out);
  nor nor_112 (nor_112_out, and_40_out, nor_113_out);
  nor nor_113 (nor_113_out, nor_112_out, RESET, and_41_out);
  nor nor_114 (nor_114_out, and_42_out, nor_115_out);
  nor nor_115 (nor_115_out, nor_114_out, RESET, and_43_out);
  nor nor_116 (nor_116_out, and_44_out, nor_117_out);
  nor nor_117 (nor_117_out, nor_116_out, RESET, and_45_out);
  not not_6 (not_6_out, nand_74_out);
  Register register_1 (.D(pull_resistor_8_node), .en(and_33_out), .clk(clock_1_out), .Q(register_1_q), .clr(RESET));
  and and_46 (and_46_out, nor_117_out, nand_74_out);
  and and_47 (and_47_out, nor_117_out, not_6_out);
  Divider divider_1 (.a(register_1_q), .b(8'ha), .out(divider_1_out), .rem(divider_1_rem));  // open: upper
  Divider divider_2 (.a(divider_1_out), .b(8'ha), .out(divider_2_out), .rem(divider_2_rem));  // open: upper
  Divider divider_3 (.a(divider_2_out), .b(8'ha), .rem(divider_3_rem));  // open: out, upper
  Hex_Digit_Display hex_digit_display_1 (.value(bitselector_3_out));  // open: dp
  BitSelector #(.group(4)) bitselector_1 (.in(divider_1_rem), .out(bitselector_1_out), .sel(1'b0));
  BitSelector #(.group(4)) bitselector_2 (.in(divider_2_rem), .out(bitselector_2_out), .sel(1'b0));
  BitSelector #(.group(4)) bitselector_3 (.in(divider_3_rem), .out(bitselector_3_out), .sel(1'b0));
  Hex_Digit_Display hex_digit_display_2 (.value(bitselector_2_out));  // open: dp
  Hex_Digit_Display hex_digit_display_3 (.value(bitselector_1_out));  // open: dp
  TTY tty_1 (.data(pull_resistor_8_node[6:0]), .clk(and_33_out), .clr(RESET));  // open: we

  // Notes on the sheet:
  //   nand_65 drives only 0 and floats otherwise
  //   nand_66 drives only 0 and floats otherwise
  //   nand_67 drives only 0 and floats otherwise
  //   nand_68 drives only 0 and floats otherwise
  //   nand_69 drives only 0 and floats otherwise
  //   nand_70 drives only 0 and floats otherwise
  //   nand_71 drives only 0 and floats otherwise
  //   nand_72 drives only 0 and floats otherwise
  //   nand_107 drives only 0 and floats otherwise
  //   nand_108 drives only 0 and floats otherwise
  //   nand_109 drives only 0 and floats otherwise
  //   nand_110 drives only 0 and floats otherwise
  //   nand_111 drives only 0 and floats otherwise
  //   nand_112 drives only 0 and floats otherwise
  //   nand_113 drives only 0 and floats otherwise
  //   nand_114 drives only 0 and floats otherwise
  //   nand_115 drives only 0 and floats otherwise
  //   nand_116 drives only 0 and floats otherwise
  //   nand_117 drives only 0 and floats otherwise
  //   nand_118 drives only 0 and floats otherwise
  //   nand_119 drives only 0 and floats otherwise
  //   OC drives only 0 and floats otherwise
  //   nand_120 drives only 0 and floats otherwise
  //   nand_121 drives only 0 and floats otherwise
endmodule
